// Logisim project Ctl_Conditional.circ as structural Verilog: 1 circuit, main circuit Conditional
module Conditional (
  input  Enable,
  input  [15:0] Instruction,
  input  Z,
  input  C,
  input  N,
  input  V,
  output [10:0] Offset,
  output Verified
);

  wire multiplexer_1_out, o_CC, o_CS, o_EQ, o_GE, o_GT, o_HI, o_LE, o_LS, o_LT, o_MI, o_NE, o_PL, o_VC, o_VS;
  wire [10:0] bit_extender_1_out;

  and and_1 (o_EQ, Z, 1'b1);
  xnor xnor_1 (o_NE, Z, 1'b0);
  and and_2 (o_CS, C, 1'b1);
  xnor xnor_2 (o_CC, C, 1'b0);
  and and_3 (o_MI, N, 1'b1);
  xnor xnor_3 (o_PL, N, 1'b1);
  and and_4 (o_VS, V, 1'b1);
  xnor xnor_4 (o_VC, V, 1'b1);
  and and_5 (o_HI, o_CS, o_NE);
  or or_1 (o_LS, o_CC, o_EQ);
  and and_6 (o_GE, N, V);
  xor xor_1 (o_LT, N, V);
  and and_7 (o_GT, o_GE, o_NE);
  or or_2 (o_LE, o_EQ, o_LT);
  Multiplexer #(.enable("false"), .select(4)) multiplexer_1 (
    .in0(o_EQ), .in1(o_NE), .in2(o_CS), .in3(o_CS), .in4(o_CC), .in5(o_CC), .in6(o_MI), .in7(o_PL),
    .in8(o_VS), .in9(o_VC), .in10(o_HI), .in11(o_LS), .in12(o_GE), .in13(o_LT), .in14(o_GT), .in15(o_LE),
    .out(multiplexer_1_out), .sel(Instruction[11:8]));
  assign bit_extender_1_out = {{3{Instruction[7]}}, Instruction[7:0]};  // Bit_Extender bit_extender_1
  Multiplexer #(.enable("false"), .width(11)) multiplexer_2 (
    .in0({11{1'b0}}), .in1(bit_extender_1_out), .out(Offset), .sel(Verified));
  and and_8 (Verified, Enable, multiplexer_1_out);

  // Other names for the same wires on the sheet: imm8[7:0] = Instruction[7:0]; cond[3:0] = Instruction[11:8];
  //   o_HS = o_CS; o_LO = o_CC
endmodule
